# Fritzing sketch fritzingsketch (saved by Fritzing 0.9.2b)
breadboards: 1

parts:
  Part1 = Arduino Uno (Rev3)
  part = Resistor [tolerance=±20% resistance=220 package=THT]
  part_2 = LED - 5mm [color="Green (570nm)" package="5 mm [THT]"]
  S1 = Pushbutton [package=THT]
  S2 = Pushbutton [package=THT]
  S3 = Pushbutton [package=THT]
  S4 = Pushbutton [package=THT]
  part_3 = Resistor [tolerance=±5% resistance=220 package=THT]
  part_4 = Resistor [tolerance=±5% resistance=220 package=THT]
  part_5 = Resistor [tolerance=±5% resistance=220 package=THT]
  part_6 = Resistor [tolerance=±5% resistance=220 package=THT]
  USB_Connected_to_PC = USB connector [package=THT]  # not connected
  D1 = Rectifier Diode [part_number=1N4001 package="300 mil [THT]"]
  D2 = Rectifier Diode [part_number=1N4001 package="300 mil [THT]"]
  D3 = Rectifier Diode [part_number=1N4001 package="300 mil [THT]"]
  D4 = Rectifier Diode [part_number=1N4001 package="300 mil [THT]"]

nets:
  N1: Part1.D8, S4.leg1, part_6.Pin_1
  N2: Part1.D13/SCK, part.Pin_0
  N3: Part1.GND, part_2.cathode, D1.cathode, D2.cathode, D3.cathode, D4.cathode
  N4: Part1.D3_PWM, S1.leg1, part_3.Pin_1
  N5: Part1.D4, S2.leg1, part_4.Pin_1
  N6: Part1.D6_PWM, S3.leg1, part_5.Pin_1
  N7: Part1.5V, S1.leg0, S2.leg0, S3.leg0, S4.leg0
  N8: part.Pin_1, part_2.anode
  N9: part_3.Pin_0, D1.anode
  N10: part_4.Pin_0, D2.anode
  N11: part_5.Pin_0, D3.anode
  N12: part_6.Pin_0, D4.anode
